# Fritzing sketch FilamentDryer (saved by Fritzing 0.9.3b)

parts:
  Часть2 = Arduino Uno (Rev3)
  KY-1 = Keyes Relay [package=THT]
  Часть3 = LCD1602-I2C
  R1 = Resistor [tolerance=±5% resistance=100k package="2512 [SMD]"]
  R2 = Temperature Sensor (Thermistor) [thermistor_type=NTC package=THT]
  Часть4 = IFR520 MOS module [package=THT]
  DS1 = DS18B20 1-Wire Temperature Sensor [part_number=DS18B20]
  SW1 = Encoder [package=encoder]
  R3 = Resistor [tolerance=±5% resistance=4.7k package="2512 [SMD]"]
  F1 = Fan - Ventilador [package=THT]

nets:
  N1: Часть2.A0, R2.pin_0
  N2: Часть2.A4/SDA, Часть3.SCL
  N3: Часть2.A5/SCL, Часть3.SDA
  N4: Часть2.D10_PWM/SS, Часть4.SIG
  N5: Часть2.D13/SCK, KY-1.signal
  N6: Часть2.GND, R2.pin_1
  N7: Часть2.D2, SW1.C
  N8: Часть2.D3_PWM, SW1.B
  N9: Часть2.D4, SW1.A
  N10: Часть2.D7, DS1.DQ, R3.Pin_0
  N11: Часть2.5V, R1.Pin_0
  N12: Часть4.V+, F1.5V
  N13: Часть4.V-, F1.GND

notes:
  NTC 3950 + 100kΩ
  DS18B20 + 4,7kΩ
  Стол 12в
  Питание 12в

custom parts:
  Keyes Relay: The Keyes 5V relay module is suitable for SCM development, home appliance control. It uses a 5V~12V TIL control signal which can control DC / AC signal.
  LCD1602-I2C: A standard character display, usually with 2x16 characters. Comes in many colors with LCM1602 IIC attached.
  Fan - Ventilador: Ventilador de 2 pines, se encuentra comunmente en computadoras de escritorio
